# Fritzing sketch Doorbell-Transmitter (saved by Fritzing 0.9.3b)
breadboards: 1

parts:
  VCC1 = Battery block 9V
  S1 = Pushbutton [package="[THT]"]
  U1 = V_REG_LD1117VXX [package=78xxl]
  KY-1 = Keyes Relay [package=THT]
  U2 = ESP8266 WiFi Module [part_number=ESP8266]
  LED1 = LED - 5mm [color="Blue (525nm)" package="5 mm [THT]"]

nets:
  GND: VCC1.-, U1.GND, KY-1.ground, U2.GND, LED1.cathode
  N1: VCC1.+, S1.Pin_3, S1.Pin_4, KY-1.C
  N2: S1.Pin_1, S1.Pin_2, U1.IN, KY-1.NO
  N3: U1.OUT, KY-1.power, U2.VCC, U2.CH_PD
  N4: KY-1.signal, U2.GPIO_2
  N5: U2.GPIO_0, LED1.anode

custom parts:
  Keyes Relay: The Keyes 5V relay module is suitable for SCM development, home appliance control. It uses a 5V~12V TIL control signal which can control DC / AC signal.
  ESP8266 WiFi Module: Generic WiFi Module based on the ESP8266 with onboard PCB antenna and UART communications
